# Fritzing sketch diagrama_esquamatico_circuito-teste-sensor-obstaculos (saved by Fritzing 0.9.2b)

parts:
  R2 = Resistor [tolerance=±5% resistance=56k package=THT]
  LED1 = smd LED [color="Red (633nm)" package="1206 [SMD]"]
  LED2 = smd LED [color="Infrared (880nm)" package="1206 [SMD]"]
  R1 = Resistor [tolerance=±5% resistance=1k package=THT]
  Componente1 = Arduino Uno (Rev3) - ICSP

nets:
  N1: R2.Pin_0, LED2.anode, Componente1.A0
  N2: R2.Pin_1, Componente1.GND
  N3: LED1.cathode, Componente1.D2
  N4: LED1.anode, R1.Pin_0
  N5: LED2.cathode, R1.Pin_1, Componente1.5V

notes:
  Sensor de obstaculos
  Infravermelho
  LED Emissor
  Foto-receptor
