# Fritzing sketch diagrama_esquamatico_sensor_obstaculos_GBK (saved by Fritzing 0.9.2b)

parts:
  R2 = Resistor [tolerance=±5% resistance=56k package=THT]
  JP1 = Header 4 [package=jst-4-pth]
  LED1 = smd LED [color="Red (633nm)" package="1206 [SMD]"]
  LED2 = smd LED [color="Infrared (880nm)" package="1206 [SMD]"]
  R1 = Resistor [tolerance=±5% resistance=1k package=THT]

nets:
  N1: R2.Pin_0, JP1.3, LED2.anode
  N2: R2.Pin_1, JP1.4
  N3: JP1.1, LED1.cathode
  N4: JP1.2, LED2.cathode, R1.Pin_1
  N5: LED1.anode, R1.Pin_0

notes:
  D2
  +5V
  A0
  GND
  Sensor de obstaculos
  Infravermelho
  LED Emissor
  Foto-receptor
